# Fritzing sketch Schemat_elektroniczny (saved by Fritzing 0.9.3b)

parts:
  Part1 = Arduino Nano (Rev3.0) (ICSP)
  Part2 = HX711 Weighing Sensor Module
  Load_Cell1 = Load Cell - Red/white/black/green
  S2 = Momentary Switch [package=ksa_sealed_tac_switch]
  Part3 = LCD1602-I2C
  BAT1 = 18650 battery holder [package=battery-18650-kit]
  BAT2 = 18650 battery holder [package=battery-18650-kit]

nets:
  GND: Part1.GND, Part2.GND, S2.2, Part3.GND, BAT1.-
  N1: Part1.D2, S2.4
  N2: Part1.D5, Part2.DO/RX
  N3: Part1.D6, Part2.CK/TX
  N4: Part1.VIN, BAT2.+
  VCC: Part1.5V, Part2.VCC, Part3.VCC
  N5: Part1.A5, Part3.SCL
  N6: Part1.A4, Part3.SDA
  N7: Part2.E+, Load_Cell1.wire1
  N8: Part2.E-, Load_Cell1.wire2
  N9: Part2.A+, Load_Cell1.wire3
  N10: Part2.A-, Load_Cell1.wire4
  N11: BAT1.+, BAT2.-

custom parts:
  Load Cell - Red/white/black/green: A rectangle load cell/weighting pressure Sensor with four wires - Red, white, black, green. Normally corresponding with E+, E-, A+, A- respectively.
  LCD1602-I2C: A standard character display, usually with 2x16 characters. Comes in many colors with LCM1602 IIC attached.
  18650 battery holder: 18650 Battery Holder
